// Logisim project BIESTABLED.circ as structural Verilog: 1 circuit, main circuit main
module main (
  input  D,
  input  Clear,
  input  Preset,
  output Q,
  output out_5
);

  wire CLK_out, nand_1_out, nand_2_out, nand_3_out, nand_4_out, not_1_out, not_2_out, not_3_out;

  Clock CLK (.out(CLK_out));
  not not_1 (not_1_out, D);
  nand nand_1 (nand_1_out, D, CLK_out);
  nand nand_2 (nand_2_out, CLK_out, not_1_out);
  nand nand_3 (nand_3_out, nand_1_out, nand_4_out);
  nand nand_4 (nand_4_out, nand_3_out, nand_2_out);
  not not_2 (not_2_out, Clear);
  not not_3 (not_3_out, Preset);
  and and_1 (Q, not_2_out, nand_3_out);
  and and_2 (out_5, nand_4_out, not_3_out);
endmodule
