// Logisim project BIESTABLERS.circ as structural Verilog: 1 circuit, main circuit main
module main (
  input  S,
  input  A,
  output Q,
  output nQ
);

  wire clock_1_out;

  Clock clock_1 (.out(clock_1_out));
  S_R_Flip_Flop s_r_ff_1 (.S(S), .clk(clock_1_out), .R(A), .Q(Q), .Qn(nQ));  // open: preset, reset, en
endmodule
