// Logisim project EjemploPractica5.circ as structural Verilog: 1 circuit, main circuit main
module main (
  input  A0,
  input  A1,
  input  B0,
  input  B1,
  output S0,
  output S1,
  output S2
);

  wire adder_1_cout;

  Adder #(.width(1)) adder_1 (.a(A0), .b(B0), .out(S0), .cin(1'b0), .cout(adder_1_cout));
  Adder #(.width(1)) adder_2 (.a(A1), .b(B1), .out(S1), .cin(adder_1_cout), .cout(S2));
  Hex_Digit_Display hex_digit_display_1 (.value({1'b0, S2, S1, S0}));  // open: dp
endmodule
