// Logisim project Ejercicio1.circ as structural Verilog: 1 circuit, main circuit main
module main (
  input  in_1,
  input  in_2,
  input  in_3,
  output out_4
);

  NotExactlyOne xnor_1 (.out(out_4), .in0(in_1), .in1(in_2), .in2(in_3));
endmodule
