// Logisim project Ejercicio3-2.circ as structural Verilog: 1 circuit, main circuit main
module main (
  input  A,
  input  B,
  input  C,
  output out_4
);

  wire and_1_out, and_2_out, not_1_out;

  not not_1 (not_1_out, A);
  and and_1 (and_1_out, A, B);
  and and_2 (and_2_out, not_1_out, C);
  or or_1 (out_4, and_1_out, and_2_out);
endmodule
