// Logisim project Ejercicio4.circ as structural Verilog: 1 circuit, main circuit main
module main (
  input  A,
  input  B,
  input  C,
  input  D,
  output out_5
);

  wire and_1_out, nand_1_out, nand_2_out, or_1_out, or_2_out;

  nand nand_1 (nand_1_out, B, C);
  nand nand_2 (nand_2_out, B, A);
  or or_1 (or_1_out, nand_1_out, D);
  and and_1 (and_1_out, A, or_1_out);
  or or_2 (or_2_out, nand_2_out, and_1_out);
  and and_2 (out_5, or_2_out, C, D);
endmodule
