// Logisim project Ejercicio5-Original.circ as structural Verilog: 1 circuit, main circuit main
module main (
  input  A,
  input  B,
  input  C,
  output out_4
);

  wire and_1_out, and_2_out, and_3_out, nor_1_out, not_1_out;

  not not_1 (not_1_out, B);
  nor nor_1 (nor_1_out, B, C);
  and and_1 (and_1_out, A, not_1_out);
  and and_2 (and_2_out, A, nor_1_out);
  and and_3 (and_3_out, B, nor_1_out);
  or or_1 (out_4, and_1_out, and_2_out, and_3_out);
endmodule
