// Logisim project Ejercicio5-p1.circ as structural Verilog: 1 circuit, main circuit main
module main (
  input  in_1,
  input  in_2,
  output out_3
);

  wire not_1_out;

  not not_1 (not_1_out, in_2);
  and and_1 (out_3, in_1, not_1_out);
endmodule
