// Logisim project Practica5-1.circ as structural Verilog: 1 circuit, main circuit main
module main (
  input  A1,
  input  A2,
  input  B1,
  input  B2,
  output S0,
  output S1,
  output S2
);

  wire subtractor_1_bout;

  Subtractor #(.width(1)) subtractor_1 (.a(A1), .b(B1), .out(S0), .bin(1'b0), .bout(subtractor_1_bout));
  Subtractor #(.width(1)) subtractor_2 (.a(A2), .b(B2), .out(S1), .bin(subtractor_1_bout), .bout(S2));
  Hex_Digit_Display hex_digit_display_1 (.value({1'b0, S2, S1, S0}));  // open: dp
endmodule
