// Logisim project Practica5-2.circ as structural Verilog: 1 circuit, main circuit main
module main (
  input  A0,
  input  A1,
  input  B0,
  input  B1,
  output S0,
  output S1,
  output S2
);

  wire and_1_out, and_2_out, and_3_out, and_4_out, and_5_out, and_6_out, and_7_out, and_8_out, and_9_out,
       and_10_out, and_11_out, not_1_out, not_2_out, not_3_out, not_4_out, not_5_out, not_6_out, not_7_out,
       not_8_out, not_9_out, not_10_out, not_11_out, not_12_out, not_13_out, not_14_out, not_15_out,
       not_16_out;

  not not_1 (not_1_out, A0);
  and and_1 (and_1_out, not_1_out, B0);
  and and_2 (and_2_out, A0, not_2_out);
  not not_2 (not_2_out, B0);
  not not_3 (not_3_out, A1);
  not not_4 (not_4_out, B0);
  not not_5 (not_5_out, A0);
  not not_6 (not_6_out, A1);
  not not_7 (not_7_out, B1);
  not not_8 (not_8_out, B0);
  not not_9 (not_9_out, B1);
  not not_10 (not_10_out, A0);
  not not_11 (not_11_out, A1);
  not not_12 (not_12_out, B1);
  not not_13 (not_13_out, A1);
  and and_3 (and_3_out, not_13_out, B1);
  not not_14 (not_14_out, A0);
  and and_4 (and_4_out, not_14_out, not_15_out, B0);
  not not_15 (not_15_out, A1);
  not not_16 (not_16_out, A0);
  and and_5 (and_5_out, not_16_out, B0, B1);
  or or_1 (S0, and_1_out, and_2_out);
  and and_6 (and_6_out, not_3_out, not_4_out, B1);
  and and_7 (and_7_out, not_5_out, not_6_out, B0, not_7_out);
  and and_8 (and_8_out, A1, not_8_out, not_9_out);
  and and_9 (and_9_out, not_10_out, A1, B0, B1);
  and and_10 (and_10_out, A0, not_11_out, B1);
  and and_11 (and_11_out, A0, A1, not_12_out);
  or or_2 (S2, and_3_out, and_4_out, and_5_out);
  or or_3 (S1, and_6_out, and_7_out, and_8_out, and_9_out, and_10_out, and_11_out);
endmodule
